# Fritzing sketch Tabla Instrument_Pcb (saved by Fritzing 0.9.3b)
circuit board: 8.46667cm x 5.64444cm
breadboards: 1

parts:
  R2 = Resistor [tolerance=±5% resistance=110 package="1206 [SMD]"]
  R3 = Resistor [tolerance=±5% resistance=110 package="1206 [SMD]"]
  R4 = Resistor [tolerance=±5% resistance=110 package="1206 [SMD]"]
  Part1 = Arduino Uno (Rev3) - ICSP
  JP2 = Header 1 [package=smtso-256-et]
  JP3 = Header 1 [package=smtso-256-et]
  JP4 = Header 1 [package=smtso-256-et]

nets:
  N1: R2.Pin_0, R3.Pin_0, R4.Pin_0, Part1.D10_PWM/SS, Part1.GND, Part1.D2, Part1.D6_PWM, JP2.1, JP3.1, JP4.1
  N2: R2.Pin_1, Part1.ICSP_MISO, Part1.D12/MISO
  N3: R3.Pin_1, Part1.D8
  N4: R4.Pin_1, Part1.D4
